// Logisim project 4 bit adder on logisim.circ as structural Verilog: 1 circuit, main circuit main
module main (
  input  I0,
  input  I1,
  input  I2,
  input  I3,
  output S0,
  output S1,
  output S2,
  output S3
);

  wire and1_out, and2_out, and3_out, and4_out, and5_out, xor1_out, xor2_out, xor3_out, xor5_out, xor7_out;

  xor xor_1 (S0, 1'b1, I0);
  and and1 (and1_out, 1'b1, I0);
  xor xor1 (xor1_out, 1'b1, I1);
  and and2 (and2_out, 1'b1, I1);
  xor xor2 (xor2_out, 1'b0, I2);
  and and3 (and3_out, 1'b0, I2);
  xor xor3 (xor3_out, 1'b0, I3);
  xor xor4 (S1, and1_out, xor1_out);
  buf and4 (and4_out, and1_out);  // AND_Gate
  or xor5 (xor5_out, and4_out, and2_out);
  xor xor6 (S2, xor5_out, xor2_out);
  and and5 (and5_out, xor5_out, xor2_out);
  or xor7 (xor7_out, and5_out, and3_out);
  xor xor8 (S3, xor7_out, xor3_out);
endmodule
